# Fritzing sketch pot-fade (saved by Fritzing 0.7.11b)
breadboards: 1

parts:
  Arduino1 = Arduino
  R1 = Rotary Potentiometer (Small) [maximum_resistance=100kΩ]
  LED1 = LED - 5mm [color="Red (633nm)" package="5 mm [THT]"]

nets:
  N1: Arduino1.GND, R1.leg1, LED1.cathode
  N2: Arduino1.D9, LED1.anode
  N3: Arduino1.+5V, R1.leg2
  N4: Arduino1.A0, R1.wiper
